# Fritzing sketch Untitled Sketch (saved by Fritzing 0.9.4)

parts:
  hc-sr1 = hc-sr04
  Parça2 = Arduino Pro Mini (5V)
  J1 = Basic Servo

nets:
  VCC: hc-sr1.VCC, Parça2.VCC, J1.vcc
  N1: hc-sr1.Trig, Parça2.D6
  N2: hc-sr1.Echo, Parça2.D5
  GND: hc-sr1.GND, Parça2.GND, J1.gnd
  N3: Parça2.D9, J1.pulse

// code stored in the sketch: Arduino.ino
#include <Servo.h>
 
// Ultrasonik Sinyal pinleri
const int trigPin = 6;
const int echoPin = 5;
 
long duration;
int distance;
char aci;
 
Servo myServo; 
 
void setup() {
  pinMode(trigPin, OUTPUT); 
  pinMode(echoPin, INPUT); 
  Serial.begin(9600);
  myServo.attach(9); // Servo motor sinyal pini
}
void loop() {
  if(Serial.available()){
    aci = Serial.read();
    if(aci < 220 && aci > 40){
      myServo.write(aci);
      delay(30); 
      distance = calculateDistance(); 
      Serial.print(distance); 
      }
    }
  }
 
int calculateDistance(){ 
   
  digitalWrite(trigPin, LOW); 
  delayMicroseconds(2);
 
  digitalWrite(trigPin, HIGH); 
  delayMicroseconds(10);
  digitalWrite(trigPin, LOW);
  duration = pulseIn(echoPin, HIGH); 
  distance= duration*0.034/2;
  return distance;
}
